# Fritzing sketch APC-UPS (saved by Fritzing 0.9.10b)

parts:
  M1 = DOIT Esp32 DevKit v1 (30 pins long, 11 pins width) [part_number=ESP32S-PIN30]
  Компонент2 = Logic Level Converter

nets:
  N1: M1.3V3, Компонент2.LV
  GND: M1.GND, Компонент2.GND
  N2: M1.RX2, Компонент2.RX_LV
  N3: M1.TX2, Компонент2.TX_LV

notes:
  GPIO17
  GPIO16
  USB Powered
  5V
  3.3V
  Level shifter
  TTL <--> RS232
  DB9 Male connector

custom parts:
  DOIT Esp32 DevKit v1 (30 pins long, 11 pins width): The DOIT Esp32 DevKit v1 is one of the development board created by DOIT to evaluate the ESP-WROOM-32 module. It is based on the ESP32 microcontroller that boasts Wifi, Bluetooth, Ethernet and Low Power support all in a single chip. (vanepp) made breadboard work, adjusted pin numbering and labels and reduced size of schematic and cleaned up pcb. This chip is 30pins long (2 x15) and 11 pins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
